// Logisim project Demux.circ as structural Verilog: 1 circuit, main circuit main
module main (
  input  I0,
  input  S1,
  input  S0,
  output O3,
  output O2,
  output O1,
  output O0
);

  wire controlled_buffer_1_out, controlled_buffer_2_out, not_1_out, not_2_out, not_3_out;

  assign controlled_buffer_1_out = S1 ? I0 : 1'bz;  // Controlled_Buffer controlled_buffer_1
  assign controlled_buffer_2_out = not_1_out ? I0 : 1'bz;  // Controlled_Buffer controlled_buffer_2
  not not_1 (not_1_out, S1);
  assign O3 = S0 ? controlled_buffer_1_out : 1'bz;  // Controlled_Buffer controlled_buffer_3
  assign O2 = not_2_out ? controlled_buffer_1_out : 1'bz;  // Controlled_Buffer controlled_buffer_4
  not not_2 (not_2_out, S0);
  not not_3 (not_3_out, S0);
  assign O1 = S0 ? controlled_buffer_2_out : 1'bz;  // Controlled_Buffer controlled_buffer_5
  assign O0 = not_3_out ? controlled_buffer_2_out : 1'bz;  // Controlled_Buffer controlled_buffer_6
endmodule
