// Logisim project Encoder.circ as structural Verilog: 1 circuit, main circuit main
module main (
  input  I3,
  input  I2,
  input  I1,
  input  I0,
  output _01,
  output O0
);

  or or_1 (O0, I3, I1);
  or or_2 (_01, I3, I2);
endmodule
