// Logisim project Register.circ as structural Verilog: 1 circuit, main circuit main
module main (
  input  CLK,
  input  D,
  input  A2,
  input  A1,
  input  A0,
  output Bit7,
  output Bit6,
  output Bit5,
  output Bit4,
  output Bit3,
  output Bit2,
  output Bit1,
  output Bit0
);

  wire controlled_buffer_1_out, dual_d_flip_flop_7474_1_p7, dual_d_flip_flop_7474_2_p2,
       dual_d_flip_flop_7474_2_p7, dual_d_flip_flop_7474_3_p2, dual_d_flip_flop_7474_3_p7,
       dual_d_flip_flop_7474_4_p2, dual_d_flip_flop_7474_4_p7, n3_to_8_decoder_74138_1_p7,
       n3_to_8_decoder_74138_1_p8, n3_to_8_decoder_74138_1_p9, n3_to_8_decoder_74138_1_p10,
       n3_to_8_decoder_74138_1_p11, n3_to_8_decoder_74138_1_p12, n3_to_8_decoder_74138_1_p13,
       n3_to_8_decoder_74138_1_p14, not_1_out, not_2_out, not_3_out, not_4_out, not_5_out, not_6_out,
       not_7_out, not_8_out;

  assign controlled_buffer_1_out = not_8_out ? D : 1'bz;  // Controlled_Buffer controlled_buffer_1
  // Dual_D_Flip_Flop__7474 #(.Facing("east")) dual_d_flip_flop_7474_1: pin names not known; wires that end beside it: 1'b1, controlled_buffer_1_out, CLK, 1'b1, Bit7, 1'b1, dual_d_flip_flop_7474_1_p7, CLK, 1'b1, Bit6
  assign dual_d_flip_flop_7474_1_p7 = not_7_out ? D : 1'bz;  // Controlled_Buffer controlled_buffer_2
  // Dual_D_Flip_Flop__7474 #(.Facing("east")) dual_d_flip_flop_7474_2: pin names not known; wires that end beside it: 1'b1, dual_d_flip_flop_7474_2_p2, CLK, 1'b1, Bit5, 1'b1, dual_d_flip_flop_7474_2_p7, CLK, 1'b1, Bit4
  assign dual_d_flip_flop_7474_2_p2 = not_6_out ? D : 1'bz;  // Controlled_Buffer controlled_buffer_3
  // _3_to_8_decoder__74138 #(.Facing("east")) 3_to_8_decoder_74138_1: pin names not known; wires that end beside it: A0, A1, A2, 1'b1, 1'b0, 1'b0, n3_to_8_decoder_74138_1_p7, n3_to_8_decoder_74138_1_p8, n3_to_8_decoder_74138_1_p9, n3_to_8_decoder_74138_1_p10, n3_to_8_decoder_74138_1_p11, n3_to_8_decoder_74138_1_p12, n3_to_8_decoder_74138_1_p13, n3_to_8_decoder_74138_1_p14
  assign dual_d_flip_flop_7474_2_p7 = not_5_out ? D : 1'bz;  // Controlled_Buffer controlled_buffer_4
  not not_1 (not_1_out, n3_to_8_decoder_74138_1_p7);
  not not_2 (not_2_out, n3_to_8_decoder_74138_1_p8);
  not not_3 (not_3_out, n3_to_8_decoder_74138_1_p9);
  not not_4 (not_4_out, n3_to_8_decoder_74138_1_p10);
  not not_5 (not_5_out, n3_to_8_decoder_74138_1_p11);
  not not_6 (not_6_out, n3_to_8_decoder_74138_1_p12);
  not not_7 (not_7_out, n3_to_8_decoder_74138_1_p13);
  not not_8 (not_8_out, n3_to_8_decoder_74138_1_p14);
  // Dual_D_Flip_Flop__7474 #(.Facing("east")) dual_d_flip_flop_7474_3: pin names not known; wires that end beside it: 1'b1, dual_d_flip_flop_7474_3_p2, CLK, 1'b1, Bit3, 1'b1, dual_d_flip_flop_7474_3_p7, CLK, 1'b1, Bit2
  assign dual_d_flip_flop_7474_3_p2 = not_4_out ? D : 1'bz;  // Controlled_Buffer controlled_buffer_5
  assign dual_d_flip_flop_7474_3_p7 = not_3_out ? D : 1'bz;  // Controlled_Buffer controlled_buffer_6
  // Dual_D_Flip_Flop__7474 #(.Facing("east")) dual_d_flip_flop_7474_4: pin names not known; wires that end beside it: 1'b1, dual_d_flip_flop_7474_4_p2, CLK, 1'b1, Bit1, 1'b1, dual_d_flip_flop_7474_4_p7, CLK, 1'b1, Bit0
  assign dual_d_flip_flop_7474_4_p2 = not_2_out ? D : 1'bz;  // Controlled_Buffer controlled_buffer_7
  assign dual_d_flip_flop_7474_4_p7 = not_1_out ? D : 1'bz;  // Controlled_Buffer controlled_buffer_8
endmodule
